# Fritzing sketch digitCounter (saved by Fritzing 0.9.3b)
breadboards: 1

parts:
  DI1 = 7-Segment LED Display [package=THT]
  DI2 = 7-Segment LED Display [package=THT]
  U1 = 74HC595 [package="DIP16 [THT]"]
  Q1 = NPN-Transistor [package="TO92 [THT]"]
  Q2 = PNP-Transistor [package="TO92 [THT]"]
  Part1 = Arduino Uno (Rev3)
  R1 = Resistor [tolerance=±5% resistance=10k package=THT]
  R2 = Resistor [tolerance=±5% resistance=330 package=THT]
  R3 = Resistor [tolerance=±5% resistance=330 package=THT]
  R4 = Resistor [tolerance=±5% resistance=330 package=THT]
  R5 = Resistor [tolerance=±5% resistance=330 package=THT]
  R6 = Resistor [tolerance=±5% resistance=330 package=THT]
  R7 = Resistor [tolerance=±5% resistance=330 package=THT]
  R8 = Resistor [tolerance=±5% resistance=220 package=THT]

nets:
  N1: DI1.cathodeE, DI2.cathodeE, R2.Pin_1
  N2: DI1.cathodeD, DI2.cathodeD, R3.Pin_1
  N3: DI1.cathodeC, DI2.cathodeC, R4.Pin_1
  N4: DI1.cathodeB, DI2.cathodeB, R5.Pin_1
  N5: DI1.cathodeA, DI2.cathodeA, R8.Pin_1
  N6: DI1.commAnode#7, Q1.E
  N7: DI1.cathodeF, DI2.cathodeF, R6.Pin_1
  N8: DI1.cathodeG, DI2.cathodeG, R7.Pin_1
  N9: DI2.commAnode#2, Q2.E
  N10: U1.Q1, R5.Pin_0
  N11: U1.Q2, R4.Pin_0
  N12: U1.Q3, R3.Pin_0
  N13: U1.Q4, R2.Pin_0
  N14: U1.Q5, R6.Pin_0
  N15: U1.Q6, R7.Pin_0
  GND: U1.GND, U1.OE, Part1.GND, R1.Pin_0
  VCC: U1.MR, U1.VCC, Q1.C, Q2.C, Part1.5V
  N16: U1.SH_CP, Part1.D4
  N17: U1.ST_CP, Part1.D3_PWM
  N18: U1.DS, Part1.D2
  N19: U1.Q0, R8.Pin_0
  N20: Q1.B, Q2.B, R1.Pin_1
